// Logisim project Controller.circ as structural Verilog: 7 circuits, main circuit main
module main (
  input  [4:0] leftYin,
  input  reset,
  input  [4:0] rightYin,
  input  scoreA,
  output [4:0] zero,
  output [4:0] ballX,
  output [4:0] ballY,
  output [4:0] leftYout,
  output [4:0] rightYout,
  output [7:0] xball,
  output [7:0] yball,
  output [7:0] vxy,
  output [7:0] scoreA_2,
  output [7:0] scoreB
);

  wire adder_2_cout, adder_3_cout, adder_6_cout, adder_7_cout, and_3_out, and_4_out, and_5_out, Bcontact,
       en1, hitA, hitB, inrange_1_sharearow, inrange_2_sharearow, not_1_out, not_2_out, not_3_out, not_4_out,
       or_1_out, or_2_out, or_4_out, xor_1_out, xor_2_out, xor_3_out, xor_4_out;
  wire [2:0] multiplexer_4_out, multiplexer_5_out, reflect_1_newv, reflect_2_newv;
  wire [4:0] from_8_to_5_bits_1_out, from_8_to_5_bits_2_out, multiplexer_2_out;
  wire [7:0] adder_1_out, adder_4_out, adder_5_out, adder_8_out, extend_1_out, extend_2_out, inc8_1_r,
       inc8_2_r, multiplexer_1_out, multiplexer_3_out;

  Adder adder_1 (.a(xball), .b(extend_1_out), .out(adder_1_out));  // open: cin, cout
  extend extend_1 (.in(vxy[2:0]), .out(extend_1_out));
  extend extend_2 (.in(vxy[5:3]), .out(extend_2_out));
  Register #(.trigger("falling")) xreg (.D(multiplexer_1_out), .en(en1), .Q(xball), .clk(scoreA));  // open: clr
  Multiplexer #(.width(8), .enable("false")) multiplexer_1 (
    .in0(adder_1_out), .in1(8'hc0), .out(multiplexer_1_out), .sel(reset));
  Adder adder_2 (.a(extend_1_out), .b(xball), .cout(adder_2_cout));  // open: out, cin
  Adder adder_3 (.a(extend_2_out), .b(yball), .cout(adder_3_cout));  // open: out, cin
  Multiplexer #(.width(5), .enable("false")) multiplexer_2 (
    .in0(rightYin), .in1(5'b01111), .out(multiplexer_2_out), .sel(reset));
  Register #(.width(5), .trigger("falling")) rightYreg (
    .D(multiplexer_2_out), .en(ballX[4]), .Q(rightYout), .clk(scoreA));  // open: clr
  Adder adder_4 (.a(xball), .b(8'he4), .out(adder_4_out));  // open: cin, cout
  Adder adder_5 (.a(xball), .b(8'h1c), .out(adder_5_out));  // open: cin, cout
  not not_1 (not_1_out, extend_1_out[7]);
  xor xor_1 (xor_1_out, extend_1_out[7], adder_2_cout);
  xor xor_2 (xor_2_out, extend_2_out[7], adder_3_cout);
  inc8 inc8_1 (.X(scoreA_2), .R(inc8_1_r));
  Register scA (.D(inc8_1_r), .en(hitA), .Q(scoreA_2), .clk(scoreA));  // open: clr
  Adder adder_6 (.a(adder_4_out), .b(extend_1_out), .cout(adder_6_cout));  // open: out, cin
  Adder adder_7 (.a(extend_1_out), .b(adder_5_out), .cout(adder_7_cout));  // open: out, cin
  and and_1 (hitB, not_1_out, xor_1_out);
  and and_2 (hitA, extend_1_out[7], xor_1_out);
  not not_2 (not_2_out, xor_1_out);
  and and_3 (and_3_out, not_2_out, not_3_out);
  not not_3 (not_3_out, Bcontact);
  Adder adder_8 (.a(yball), .b(extend_2_out), .out(adder_8_out));  // open: cin, cout
  not not_4 (not_4_out, xor_2_out);
  Multiplexer #(.width(8), .enable("false")) multiplexer_3 (
    .in0(adder_8_out), .in1(8'h80), .out(multiplexer_3_out), .sel(reset));
  or or_1 (or_1_out, not_4_out, reset);
  inc8 inc8_2 (.X(scoreB), .R(inc8_2_r));
  from_8_to_5_bits from_8_to_5_bits_1 (.in(yball), .out(from_8_to_5_bits_1_out));
  xor xor_3 (xor_3_out, adder_6_cout, extend_1_out[7]);
  xor xor_4 (xor_4_out, adder_7_cout, extend_1_out[7]);
  or or_2 (or_2_out, reset, Bcontact, xor_1_out);
  or or_3 (en1, and_3_out, reset);
  Register #(.trigger("falling")) yreg (.D(multiplexer_3_out), .en(or_1_out), .Q(yball), .clk(scoreA));  // open: clr
  Register scB (.D(inc8_2_r), .en(hitB), .Q(scoreB), .clk(scoreA));  // open: clr
  inrange inrange_1 (.Yball(from_8_to_5_bits_2_out), .Ybat(rightYin), .shareArow(inrange_1_sharearow));
  from_8_to_5_bits from_8_to_5_bits_2 (.in(yball), .out(from_8_to_5_bits_2_out));
  reflect reflect_1 (.oldv(vxy[2:0]), .newv(reflect_1_newv));
  reflect reflect_2 (.oldv(vxy[5:3]), .newv(reflect_2_newv));
  inrange inrange_2 (.Yball(from_8_to_5_bits_1_out), .Ybat(leftYin), .shareArow(inrange_2_sharearow));
  Multiplexer #(.width(3), .enable("false")) multiplexer_4 (
    .in0(reflect_1_newv), .in1(3'b110), .out(multiplexer_4_out), .sel(reset));
  Multiplexer #(.width(3), .enable("false")) multiplexer_5 (
    .in0(reflect_2_newv), .in1(3'b001), .out(multiplexer_5_out), .sel(reset));
  or or_4 (or_4_out, xor_2_out, reset);
  and and_4 (and_4_out, inrange_2_sharearow, xor_3_out);
  and and_5 (and_5_out, inrange_1_sharearow, xor_4_out);
  Register #(.width(3)) vx (.D(multiplexer_4_out), .en(or_2_out), .Q(vxy[2:0]), .clk(scoreA));  // open: clr
  Register #(.width(3)) vy (.D(multiplexer_5_out), .en(or_4_out), .Q(vxy[5:3]), .clk(scoreA));  // open: clr
  or or_5 (Bcontact, and_4_out, and_5_out);
  from_8_to_5_bits from_8_to_5_bits_3 (.in(xball), .out(ballX));
  from_8_to_5_bits from_8_to_5_bits_4 (.in(yball), .out(ballY));

  assign leftYout = leftYin;
  assign vxy[7:6] = 2'b00;
  assign zero = {5{1'b0}};

  // Other names for the same wires on the sheet: clock = scoreA; LeftBat[4:0] = leftYin; RightBat[4:0] = rightYout;
  //   vx[2:0] = vxy[2:0]; vy[2:0] = vxy[5:3]; xreg[7:0] = xball; yreg[7:0] = yball

  // Notes on the sheet:
  //   longVX
  //   longVY
  //   yxneg
  //   vxneg
  //   xrefl
  //   yrefl
  //   hitB
  //   hitA
  //   LBcontact
  //   RBcontact
  //   Bcontact
endmodule

module reflect (
  input  [2:0] oldv,
  output [2:0] newv
);

  wire comparator_1_eq;
  wire [2:0] inc3_1_r, not_1_out;

  Comparator #(.width(3)) comparator_1 (.a(3'b100), .b(oldv), .eq(comparator_1_eq));  // open: gt, lt
  assign not_1_out = ~oldv;  // NOT_Gate not_1, 3 bits wide
  inc3 inc3_1 (.X(not_1_out), .R(inc3_1_r));
  Multiplexer #(.width(3), .enable("false")) multiplexer_1 (
    .in0(inc3_1_r), .in1(not_1_out), .out(newv), .sel(comparator_1_eq));
endmodule

module inc3 (
  input  [2:0] X,
  output [2:0] R
);

  wire [2:1] and_1_out;
  wire [2:2] and_1_out_2;

  assign {and_1_out_2[2], and_1_out} = {and_1_out, 1'b1} & X;  // AND_Gate and_1, 3 bits wide
  assign R = X ^ {and_1_out, 1'b1};  // XOR_Gate xor_1, 3 bits wide
  // Probe on and_1_out_2[2]
endmodule

module inrange (
  input  [4:0] Yball,
  input  [4:0] Ybat,
  output shareArow
);

  wire comparator_1_eq, comparator_2_eq, comparator_3_eq;
  wire [4:0] adder_1_out, adder_2_out;

  Adder #(.width(5)) adder_1 (.a(Ybat), .b(5'b00001), .out(adder_1_out));  // open: cin, cout
  Adder #(.width(5)) adder_2 (.a(Ybat), .b(5'b00010), .out(adder_2_out));  // open: cin, cout
  Comparator #(.width(5)) comparator_1 (.a(Yball), .b(Ybat), .eq(comparator_1_eq));  // open: gt, lt
  Comparator #(.width(5)) comparator_2 (.a(Yball), .b(adder_1_out), .eq(comparator_2_eq));  // open: gt, lt
  Comparator #(.width(5)) comparator_3 (.a(Yball), .b(adder_2_out), .eq(comparator_3_eq));  // open: gt, lt
  or or_1 (shareArow, comparator_1_eq, comparator_2_eq, comparator_3_eq);
endmodule

module extend (
  input  [2:0] in,
  output [7:0] out
);

  wire comparator_1_eq, comparator_1_gt, or_1_out;

  // Probe on in
  Comparator #(.width(3)) comparator_1 (.a(in), .b(3'b000), .gt(comparator_1_gt), .eq(comparator_1_eq));  // open: lt
  or or_1 (or_1_out, comparator_1_gt, comparator_1_eq);
  Multiplexer #(.enable("false")) multiplexer_1 (.in0(1'b1), .in1(1'b0), .out(out[7]), .sel(or_1_out));
  // Probe on {{5{out[7]}}, in}

  assign out[6:0] = {{4{out[7]}}, in};
endmodule

module from_8_to_5_bits (
  input  [7:0] in,
  output [4:0] out
);


  assign out = in[7:3];
endmodule

module inc8 (
  input  [7:0] X,
  output [7:0] R
);

  wire [7:1] and_1_out;
  wire [7:7] and_1_out_2;

  assign {and_1_out_2[7], and_1_out} = {and_1_out, 1'b1} & X;  // AND_Gate and_1, 8 bits wide
  assign R = X ^ {and_1_out, 1'b1};  // XOR_Gate xor_1, 8 bits wide
  // Probe on and_1_out_2[7]
endmodule
